// Logisim project tutorial0.circ as structural Verilog: 4 circuits, main circuit main
module main (
  input  A,
  input  B,
  input  Cin,
  output Sum,
  output Cout
);

  add_binary add_binary_1 (.A(A), .B(B), .Cin(Cin), .Sum(Sum), .Cout(Cout));
endmodule

module add_binary (
  input  A,
  input  B,
  input  Cin,
  output Sum,
  output Cout
);

  wire and_1_out, and_2_out, xor_1_out, xor_2_out;

  xor xor_1 (xor_1_out, A, B);
  xor xor_2 (xor_2_out, A, B);
  and and_1 (and_1_out, B, A);
  and and_2 (and_2_out, xor_2_out, Cin);
  xor xor_3 (Sum, xor_1_out, Cin);
  or or_1 (Cout, and_1_out, and_2_out);
endmodule

module add_eight (
  input  A,
  input  B,
  output [7:0] out_3
);

  wire add_binary_1_cout, add_binary_2_cout, add_binary_3_cout, add_binary_4_cout, add_binary_5_cout,
       add_binary_6_cout, add_binary_7_cout, add_binary_8_cout, undriven;

  add_binary add_binary_1 (.A(A), .B(B), .Cin(undriven), .Sum(out_3[0]), .Cout(add_binary_1_cout));
  add_binary add_binary_2 (.A(A), .B(B), .Cin(add_binary_1_cout), .Sum(out_3[1]), .Cout(add_binary_2_cout));
  add_binary add_binary_3 (.A(A), .B(B), .Cin(add_binary_2_cout), .Sum(out_3[2]), .Cout(add_binary_3_cout));
  add_binary add_binary_4 (.A(A), .B(B), .Cin(add_binary_3_cout), .Sum(out_3[3]), .Cout(add_binary_4_cout));
  add_binary add_binary_5 (.A(A), .B(B), .Cin(add_binary_4_cout), .Sum(out_3[4]), .Cout(add_binary_5_cout));
  add_binary add_binary_6 (.A(A), .B(B), .Cin(add_binary_5_cout), .Sum(out_3[5]), .Cout(add_binary_6_cout));
  add_binary add_binary_7 (.A(A), .B(B), .Cin(add_binary_6_cout), .Sum(out_3[6]), .Cout(add_binary_7_cout));
  add_binary add_binary_8 (.A(A), .B(B), .Cin(add_binary_7_cout), .Sum(out_3[7]), .Cout(add_binary_8_cout));
endmodule

module test_eight (
);

  add_eight add_eight_1 ();  // open: A, B, out_3
endmodule
