// Logisim project cpu.circ as structural Verilog: 4 circuits, main circuit CPU
module CPU (
  output [47:0] cpu_out,
  output halt
);

  wire and_4_out, and_7_out, and_9_out, and_10_out, branch_condition_true, branch_taken, C, clk,
       comparator_7_eq, comparator_8_eq, comparator_9_eq, comparator_11_eq, EQ, fsm_execute, GE, GT, ir_we,
       is_branch, LE, load, LT, N, NE, not_1_out, or_1_out, or_3_out, pc_we_part5, ra_we,
       ram_mem_stage_and_store, rd_we, reset, reset_fsm, rf_we, rf_we_register, rw_we, Store, undriven, V,
       xnor_2_out;
  wire [2:0] adder_2_out, addr_b, multiplexer_2_out, Mux_equals4, next_state_part5, state_reg;
  wire [15:0] adder_1_out, alu_mult_c, bit_extender_1_out, bit_extender_2_out, InsMem_data,
       multiplexer_1_out, multiplexer_4_out, MuxOut, RA_q, ram_out, RbQ, rd_q, registerfile_1_a,
       registerfile_1_b, RwQ;

  Clock u_clk (.out(clk));
  Button u_reset (.out(reset));
  Comparator #(.width(3)) comparator_1 (.a(state_reg), .b(3'b011), .eq(fsm_execute));  // open: gt, lt
  Comparator #(.width(3)) comparator_2 (.a(state_reg), .b(3'b000), .eq(ir_we));  // open: gt, lt
  Comparator #(.width(3)) comparator_3 (.a(state_reg), .b(3'b001), .eq(ra_we));  // open: gt, lt
  Comparator #(.width(3)) comparator_4 (.a(state_reg), .b(3'b010), .eq(rd_we));  // open: gt, lt
  Comparator #(.width(3)) comparator_5 (.a(state_reg), .b(3'b011), .eq(rw_we));  // open: gt, lt
  Comparator #(.width(3)) comparator_6 (.a(state_reg), .b(3'b100), .eq(rf_we));  // open: gt, lt
  Comparator #(.width(3)) comparator_7 (.a(state_reg), .b(3'b011), .eq(comparator_7_eq));  // open: gt, lt
  Comparator #(.width(2)) comparator_8 (.a(cpu_out[31:30]), .b(2'b11), .eq(comparator_8_eq));  // open: gt, lt
  Comparator #(.width(2)) comparator_9 (.a(cpu_out[31:30]), .b(2'b01), .eq(comparator_9_eq));  // open: gt, lt
  not not_1 (not_1_out, cpu_out[31]);
  and and_1 (ram_mem_stage_and_store, comparator_7_eq, comparator_8_eq);
  Register #(.width(16)) PC (.D(adder_1_out), .en(pc_we_part5), .clk(clk), .Q(cpu_out[47:32]), .clr(reset));
  and and_2 (Store, cpu_out[30], cpu_out[31]);
  and and_3 (is_branch, cpu_out[30], not_1_out);
  RAM #(.addrWidth(16), .dataWidth(16), .enables("line")) ram_mem (
    .addr(cpu_out[15:0]), .we(ram_mem_stage_and_store), .clk(clk), .din(rd_q), .dout(ram_out));
  assign bit_extender_1_out = {{13{cpu_out[25]}}, cpu_out[25:23]};  // Bit_Extender bit_extender_1
  and and_4 (and_4_out, fsm_execute, branch_taken);
  and and_5 (load, ~cpu_out[30], cpu_out[31]);  // AND_Gate
  Multiplexer #(.width(16)) multiplexer_1 (
    .in0(16'h1), .in1(bit_extender_1_out), .out(multiplexer_1_out), .sel(and_4_out));
  ROM #(.addrWidth(16), .dataWidth(16)) InsMem (.addr(cpu_out[47:32]), .data(InsMem_data));
  RegisterFile registerfile_1 (
    .Addr_A(cpu_out[22:20]), .Addr_B(addr_b), .Addr_C(cpu_out[25:23]), .we(rf_we_register), .clk(clk),
    .reset(reset), .C(RwQ), .A(registerfile_1_a), .B(registerfile_1_b));
  Adder #(.width(16)) adder_1 (.a(cpu_out[47:32]), .b(multiplexer_1_out), .out(adder_1_out), .cin(1'b0));  // open: cout
  and and_6 (rf_we_register, ~Store, ~is_branch, rf_we);  // AND_Gate
  Register #(.width(16)) RA (.D(registerfile_1_a), .en(ra_we), .clk(clk), .Q(RA_q), .clr(reset));
  Register #(.width(16)) RB (.D(registerfile_1_b), .en(ra_we), .clk(clk), .Q(RbQ), .clr(reset));
  Register #(.width(16)) IR (.D(InsMem_data), .en(ir_we), .clk(clk), .Q(cpu_out[31:16]), .clr(reset));
  Register #(.width(16)) RD (.D(RbQ), .en(rd_we), .clk(clk), .Q(rd_q), .clr(reset));
  and and_7 (and_7_out, branch_taken, fsm_execute, is_branch);
  Multiplexer #(.width(3)) multiplexer_2 (.in0(cpu_out[29:27]), .in1(3'b001), .out(multiplexer_2_out), .sel(is_branch));
  or or_1 (or_1_out, ir_we, and_7_out);
  ALU alu_mult (
    .A(RA_q), .B(MuxOut), .fun(multiplexer_2_out), .negative(N), .zero(EQ), .carry(C), .overflow(V),
    .C(alu_mult_c));
  Register #(.width(3)) u_state_reg (.D(Mux_equals4), .en(1'b1), .clk(clk), .Q(state_reg), .clr(reset));
  Multiplexer #(.select(2), .width(3)) multiplexer_3 (
    .in0(cpu_out[18:16]), .in1(cpu_out[18:16]), .in2(cpu_out[18:16]), .in3(cpu_out[25:23]), .out(addr_b),
    .sel(cpu_out[31:30]));
  Comparator #(.width(16)) comparator_10 (.a(cpu_out[31:16]), .b(16'h4380), .eq(halt));  // open: gt, lt
  not not_2 (NE, EQ);
  Register #(.width(16)) RZ (.D(alu_mult_c), .en(rd_we), .clk(clk), .Q(cpu_out[15:0]), .clr(reset));
  Adder #(.width(3)) adder_2 (.a(state_reg), .b(3'b001), .out(adder_2_out));  // open: cin, cout
  xor xor_1 (LT, N, V);
  xnor xnor_1 (GE, N, V);
  assign bit_extender_2_out = {{12{cpu_out[19]}}, cpu_out[19:16]};  // Bit_Extender bit_extender_2
  Multiplexer #(.width(16)) multiplexer_4 (.in0(cpu_out[15:0]), .in1(ram_out), .out(multiplexer_4_out), .sel(load));
  Comparator #(.width(3)) comparator_11 (.a(adder_2_out), .b(3'b101), .eq(comparator_11_eq));  // open: gt, lt
  or or_2 (LE, EQ, LT);
  xnor xnor_2 (xnor_2_out, N, V);
  Register #(.width(16)) RW (.D(multiplexer_4_out), .en(rw_we), .clk(clk), .Q(RwQ), .clr(reset));
  Multiplexer #(.width(16)) multiplexer_5 (.in0(RbQ), .in1(bit_extender_2_out), .out(MuxOut), .sel(cpu_out[26]));
  Multiplexer #(.width(3)) multiplexer_6 (.in0(adder_2_out), .in1(3'b000), .out(Mux_equals4), .sel(or_3_out));
  or or_3 (or_3_out, comparator_11_eq, and_9_out);
  and and_8 (GT, NE, xnor_2_out);
  and and_9 (and_9_out, fsm_execute, branch_taken);
  and and_10 (and_10_out, fsm_execute, branch_taken);
  Multiplexer #(.width(3)) multiplexer_7 (.in0(Mux_equals4), .in1(3'b000), .out(next_state_part5), .sel(and_9_out));
  or or_4 (pc_we_part5, ir_we, and_10_out);
  Multiplexer #(.select(3)) multiplexer_8 (
    .in0(EQ), .in1(NE), .in2(LT), .in3(LE), .in4(GT), .in5(GE), .in7(undriven), .out(branch_condition_true),
    .sel(cpu_out[29:27]));  // open: in6
  or or_5 (reset_fsm, and_10_out, reset);
  and and_11 (branch_taken, is_branch, branch_condition_true);

  // Other names for the same wires on the sheet: rz_q[15:0] = cpu_out[15:0]; ir_q[15:0] = cpu_out[31:16];
  //   SrcReg1[2:0] = cpu_out[22:20]; DestReg[2:0] = cpu_out[25:23]; I = cpu_out[26]; AluOp[2:0] = cpu_out[29:27];
  //   Opcode[1:0] = cpu_out[31:30]; pc_q[15:0] = cpu_out[47:32]; pc_we = ir_we; rb_we = ra_we; rz_we = rd_we; Z = EQ

  // Notes on the sheet:
  //   contents of InsMem (hex, n*v repeats v):
  //   490 6d90 2091 491 401 52d 6da0 2122 521 401 15b0 16d0 1621 4540 4e50 1b1 2c91 4e50 3521 2d2 4e50
  //   4d01 21b3 5b1 5b0 4380
endmodule

module ALU (
  input  [2:0] fun,
  input  [15:0] A,
  input  [15:0] B,
  output [15:0] C,
  output negative,
  output zero,
  output carry,
  output overflow
);

  wire xnor_1_out, xor_1_out;
  wire [15:0] adder_1_out, and_1_out, multiplexer_1_out, nor_1_out, not_1_out, or_1_out, shifter_1_out,
       shifter_2_out, shifter_3_out;

  assign not_1_out = ~B;  // NOT_Gate not_1, 16 bits wide
  assign and_1_out = A & B;  // AND_Gate and_1, 16 bits wide
  assign or_1_out = A | B;  // OR_Gate or_1, 16 bits wide
  assign nor_1_out = ~(A | B);  // NOR_Gate nor_1, 16 bits wide
  Multiplexer #(.width(16)) multiplexer_1 (.in0(B), .in1(not_1_out), .out(multiplexer_1_out), .sel(fun[0]));
  Shifter #(.width(16)) shifter_1 (.in(A), .\dist (B[3:0]), .out(shifter_1_out));
  Adder #(.width(16)) adder_1 (.a(A), .b(multiplexer_1_out), .out(adder_1_out), .cin(fun[0]), .cout(carry));
  Multiplexer #(.select(3), .width(16)) multiplexer_2 (
    .in0(adder_1_out), .in1(adder_1_out), .in2(and_1_out), .in3(or_1_out), .in4(nor_1_out),
    .in5(shifter_1_out), .in6(shifter_2_out), .in7(shifter_3_out), .out(C), .sel(fun));
  Shifter #(.shift("lr"), .width(16)) shifter_2 (.in(A), .\dist (B[3:0]), .out(shifter_2_out));
  Shifter #(.shift("ar"), .width(16)) shifter_3 (.in(A), .\dist (B[3:0]), .out(shifter_3_out));
  Comparator #(.width(16)) comparator_1 (.a(C), .b({16{1'b0}}), .eq(zero));  // open: gt, lt
  xnor xnor_1 (xnor_1_out, A[15], multiplexer_1_out[15]);
  xor xor_1 (xor_1_out, adder_1_out[15], A[15]);
  and and_2 (overflow, xnor_1_out, xor_1_out);

  assign negative = C[15];
endmodule

module RegisterFile (
  input  [2:0] Addr_A,
  input  [2:0] Addr_B,
  input  [2:0] Addr_C,
  input  we,
  input  clk,
  input  reset,
  input  [15:0] C,
  output [15:0] A,
  output [15:0] B
);

  wire and_1_out, and_2_out, and_3_out, and_4_out, and_5_out, and_6_out, and_7_out, and_8_out,
       decoder_1_out0, decoder_1_out1, decoder_1_out2, decoder_1_out3, decoder_1_out4, decoder_1_out5,
       decoder_1_out6, decoder_1_out7;
  wire [15:0] R0_q, R1_q, R2_q, R3_q, R4_q, R5_q, R6_q, R7_q;

  Register #(.width(16)) R0 (.D(C), .en(and_1_out), .clk(clk), .Q(R0_q), .clr(reset));
  Register #(.width(16)) R1 (.D(C), .en(and_2_out), .clk(clk), .Q(R1_q), .clr(reset));
  Register #(.width(16)) R2 (.D(C), .en(and_3_out), .clk(clk), .Q(R2_q), .clr(reset));
  Register #(.width(16)) R3 (.D(C), .en(and_4_out), .clk(clk), .Q(R3_q), .clr(reset));
  Register #(.width(16)) R4 (.D(C), .en(and_5_out), .clk(clk), .Q(R4_q), .clr(reset));
  Register #(.width(16)) R5 (.D(C), .en(and_6_out), .clk(clk), .Q(R5_q), .clr(reset));
  Register #(.width(16)) R6 (.D(C), .en(and_7_out), .clk(clk), .Q(R6_q), .clr(reset));
  Register #(.width(16)) R7 (.D(C), .en(and_8_out), .clk(clk), .Q(R7_q), .clr(reset));
  Multiplexer #(.select(3), .width(16)) multiplexer_1 (
    .in0(R0_q), .in1(R1_q), .in2(R2_q), .in3(R3_q), .in4(R4_q), .in5(R5_q), .in6(R6_q), .in7(R7_q), .out(A),
    .sel(Addr_A));
  Decoder #(.enable("false"), .select(3)) decoder_1 (
    .out0(decoder_1_out0), .out1(decoder_1_out1), .out2(decoder_1_out2), .out3(decoder_1_out3),
    .out4(decoder_1_out4), .out5(decoder_1_out5), .out6(decoder_1_out6), .out7(decoder_1_out7), .sel(Addr_C));
  Multiplexer #(.select(3), .width(16)) multiplexer_2 (
    .in0(R0_q), .in1(R1_q), .in2(R2_q), .in3(R3_q), .in4(R4_q), .in5(R5_q), .in6(R6_q), .in7(R7_q), .out(B),
    .sel(Addr_B));
  and and_1 (and_1_out, we, decoder_1_out0);
  and and_2 (and_2_out, we, decoder_1_out1);
  and and_3 (and_3_out, we, decoder_1_out2);
  and and_4 (and_4_out, we, decoder_1_out3);
  and and_5 (and_5_out, we, decoder_1_out4);
  and and_6 (and_6_out, we, decoder_1_out5);
  and and_7 (and_7_out, we, decoder_1_out6);
  and and_8 (and_8_out, we, decoder_1_out7);
endmodule

module RegisterFileTester (
  output halt,
  output [15:0] A,
  output [15:0] B,
  output clk
);

  wire undriven;
  wire [2:0] Addr_A_data, Addr_B_data, Addr_C_data;
  wire [3:0] adder_1_out, addr_q;
  wire [15:0] C_data;

  Clock clock_1 (.out(clk));
  ROM #(.addrWidth(4), .dataWidth(3)) Addr_A (.addr(addr_q), .data(Addr_A_data));
  ROM #(.addrWidth(4), .dataWidth(3)) Addr_B (.addr(addr_q), .data(Addr_B_data));
  ROM #(.addrWidth(4), .dataWidth(3)) Addr_C (.addr(addr_q), .data(Addr_C_data));
  ROM #(.addrWidth(4), .dataWidth(1)) we (.addr(addr_q));  // open: data
  ROM #(.addrWidth(4), .dataWidth(16)) C (.addr(addr_q), .data(C_data));
  Adder #(.width(4)) adder_1 (.a(addr_q), .b(4'b0001), .out(adder_1_out), .cin(1'b0));  // open: cout
  Register #(.width(4)) addr (.D(adder_1_out), .en(1'b1), .clk(clk), .Q(addr_q), .clr(1'b0));
  Comparator #(.width(4)) comparator_1 (.a(addr_q), .b(4'b1111), .eq(halt));  // open: gt, lt
  RegisterFile registerfile_1 (
    .Addr_A(Addr_A_data), .Addr_B(Addr_B_data), .Addr_C(Addr_C_data), .we(undriven), .clk(clk), .reset(1'b0),
    .C(C_data), .A(A), .B(B));

  // Notes on the sheet:
  //   contents of Addr_A (hex, n*v repeats v):
  //   5 2 7 3 2 0 2 6 2 4 1 3 5 5 2 6
  //   contents of Addr_B (hex, n*v repeats v):
  //   4 4 6 0 2 3 5 5 5 0 0 4 5 3 7 5
  //   contents of Addr_C (hex, n*v repeats v):
  //   0 5 0 5 5 7 2 3 6 4 0 4 7 7 4 6
  //   contents of we (hex, n*v repeats v):
  //   0 0 0 1 0 0 1 0 0 0 1 1 0 0 1 1
  //   contents of C (hex, n*v repeats v):
  //   1 4 c f 0 5 9 7 c b 9 f b 9 1 e
endmodule
